# Fritzing sketch Wiring (saved by Fritzing 0.9.3b)

parts:
  S1 = H-Bridge with L298N
  Raspberry_Pi_1 = Raspberry Pi 4 [part_number=RPI-4-b]  # not connected
  Part1 = Arduino Mega 2560 (Rev3)
  Right = DC Motor with two-phase hall-encoder
  Left = DC Motor with two-phase hall-encoder

nets:
  N1: S1.ENA, Part1.A3
  N2: S1.IN1, Part1.D8_PWM
  N3: S1.IN2, Part1.D9_PWM
  N4: S1.IN3, Part1.D4_PWM
  N5: S1.IN4, Part1.D5_PWM
  N6: S1.ENB, Part1.A2
  N7: S1.M1-01, Left.pin2
  N8: S1.M1-02, Left.pin1
  N9: S1.M2-01, Right.pin2
  N10: S1.M2-02, Right.pin1
  N11: Part1.D19/RX1, Left.pin3
  N12: Part1.D18/TX1, Left.pin6
  N13: Part1.GND, Right.pin4, Left.pin4
  N14: Part1.5V, Right.pin5, Left.pin5
  N15: Part1.D2_PWM, Right.pin6
  N16: Part1.D3_PWM, Right.pin3

custom parts:
  H-Bridge with L298N: h-bridge
  Raspberry Pi 4: The RPi4, a faster version of the awesome Raspberry Pi 2 B ARM Board with 40 pin gpio. Ready for special Raspberry Pi B+ and RPi2 Hat (Hardware attached (on) top)
