# Fritzing sketch Wiring (saved by Fritzing 0.9.3b)

parts:
  S1 = H-Bridge with L298N
  Arduino_Mega_2560 = Arduino Mega 2560 (Rev3)
  Right = DC Motor with two-phase hall-encoder
  Left = DC Motor with two-phase hall-encoder
  OLED = OLED 128x64 I2C Monochrome Display
  Fan = Fan - Ventilador [package=THT]
  MPU6050 = MPU-6050 Board GY-521 [form="♀ (female)" package=THT]
  Power_plug1 = USB-C plug
  USBTTL1 = Micro USB B Plug
  USBTTL2 = USB A Plug
  part = Resistor [tolerance=±5% resistance=64.9k package=THT]
  part_2 = Resistor [tolerance=±5% resistance=100k package=THT]
  part_3 = Resistor [tolerance=±5% resistance=64.9k package=THT]
  part_4 = Resistor [tolerance=±5% resistance=100k package=THT]
  BAT1 = LIPO-2000mAh [package=lipo-2000]
  BAT2 = LIPO-2000mAh [package=lipo-2000]
  Raspberry_Pi_4B = Raspberry Pi 4 [part_number=RPI-4-b]
  Step-down_voltage_regualtor = Voltage Regulator LM1117 [package=sot223]
  Joystick_USB_dongle = USB A Plug  # not connected

nets:
  N1: S1.12V, part_2.Pin_0, BAT1.+
  N2: S1.GND, part.Pin_1, BAT1.-
  N3: S1.ENA, S1.ENA-5V, Arduino_Mega_2560.D8_PWM
  N4: S1.IN1, Arduino_Mega_2560.D9_PWM
  N5: S1.IN2, Arduino_Mega_2560.D10_PWM
  N6: S1.IN3, Arduino_Mega_2560.D11_PWM
  N7: S1.IN4, Arduino_Mega_2560.D12_PWM
  N8: S1.ENB, S1.ENB-5V, Arduino_Mega_2560.D13_PWM
  N9: S1.M1-01, Left.pin2
  N10: S1.M1-02, Left.pin1
  N11: S1.M2-01, Right.pin2
  N12: S1.M2-02, Right.pin1
  N13: Arduino_Mega_2560.A0, part_3.Pin_0, part_4.Pin_1
  N14: Arduino_Mega_2560.A2, part.Pin_0, part_2.Pin_1
  N15: Arduino_Mega_2560.D21/SCL, MPU6050.pin3
  N16: Arduino_Mega_2560.D20/SDA, Arduino_Mega_2560.SDA, MPU6050.pin4, MPU6050.pin5
  N17: Arduino_Mega_2560.D19/RX1, Left.pin3
  N18: Arduino_Mega_2560.D18/TX1, Left.pin6
  N19: Arduino_Mega_2560.GND, Right.pin4, Left.pin4, MPU6050.pin2
  N20: Arduino_Mega_2560.D2_PWM, Right.pin3
  N21: Arduino_Mega_2560.D3_PWM, Right.pin6
  N22: Arduino_Mega_2560.5V, Right.pin5, Left.pin5, MPU6050.pin1
  GND: OLED.GND, Fan.GND, Raspberry_Pi_4B.GPIO17, Raspberry_Pi_4B.GPIO27, Raspberry_Pi_4B.GND, Raspberry_Pi_4B.GPIO18
  N23: OLED.SCK, Raspberry_Pi_4B.GPIO3
  N24: OLED.SDA, Raspberry_Pi_4B.GPIO2
  5V: Fan.5V, Raspberry_Pi_4B.5V
  N25: Power_plug1.GND, part_4.Pin_0, BAT2.+, Step-down_voltage_regualtor.OUT
  N26: Power_plug1.VCC, Step-down_voltage_regualtor.ADJ
  N27: USBTTL1.usb, USBTTL2.usb
  N28: part_3.Pin_1, BAT2.-, Step-down_voltage_regualtor.IN

custom parts:
  H-Bridge with L298N: h-bridge
  Fan - Ventilador: Ventilador de 2 pines, se encuentra comunmente en computadoras de escritorio
  MPU-6050 Board GY-521: Acelerometro y Giroscopio MPU-6050 Board GY-521
  USB-C plug: power plug
  Raspberry Pi 4: The RPi4, a faster version of the awesome Raspberry Pi 2 B ARM Board with 40 pin gpio. Ready for special Raspberry Pi B+ and RPi2 Hat (Hardware attached (on) top)
